// Logisim project LedRGB.circ as structural Verilog: 3 circuits, main circuit main
module main (
  input  [3:0] Rdif
);

  wire [7:0] and_1_out, divisor_1_out_azul, divisor_1_out_vermelho;

  Divisor divisor_1 (.in_1(Rdif), .in_2(Rdif), .OUT_Vermelho(divisor_1_out_vermelho), .OUT_Azul(divisor_1_out_azul));
  assign and_1_out = {8{1'b1}} & divisor_1_out_vermelho;  // AND_Gate and_1, 8 bits wide
  // RGBLed #(.multibit("true")) LED_VERDE: pin names not known; wires that end beside it: and_1_out
  // RGBLed #(.multibit("true")) LED: pin names not known; wires that end beside it: divisor_1_out_vermelho, divisor_1_out_azul

  // Notes on the sheet:
  //   and_1 drives only 1 and floats otherwise
endmodule

module Divisor (
  input  [3:0] in_1,
  input  [3:0] in_2,
  output [7:0] OUT_Vermelho,
  output [7:0] OUT_Azul
);

  assign OUT_Vermelho[7:4] = ~in_1;  // NOT_Gate not_1, 4 bits wide

  assign OUT_Azul = {in_2, 4'b0000};
  assign OUT_Vermelho[3:0] = 4'b1111;
endmodule

module LED_RGB (
  input  [3:0] Rdif
);

  wire [7:0] and_1_out, divisor_1_out_azul, divisor_1_out_vermelho;

  Divisor divisor_1 (.in_1(Rdif), .in_2(Rdif), .OUT_Vermelho(divisor_1_out_vermelho), .OUT_Azul(divisor_1_out_azul));
  assign and_1_out = {8{1'b1}} & divisor_1_out_vermelho;  // AND_Gate and_1, 8 bits wide
  // RGBLed #(.multibit("true")) rgbled_1: pin names not known; wires that end beside it: and_1_out
  // RGBLed #(.multibit("true")) LED: pin names not known; wires that end beside it: divisor_1_out_vermelho, divisor_1_out_azul

  // Notes on the sheet:
  //   and_1 drives only 1 and floats otherwise
endmodule
